// Digital circuit cpu.dig as structural Verilog
module cpu (
  input  CLK
);

  wire EXEC, FLEN, I_mem, LDR, SETH, STR, WE, Z;
  wire [1:0] ALUOP, DMUX;
  wire [2:0] RS1, RS2, WS;
  wire [3:0] alu_1_flag;
  wire [7:0] control_unit_1_p2;
  wire [15:0] alu_1_result, i_mem_1__1a, multiplexer_1_out, notconnected_1_out, RAM_d1, reg_file_1_out1,
       reg_file_1_out2, reg_file_1_pc;
  wire [15:1] FL_q;
  wire [15:8] control_unit_1_p2_2;

  // control_unit control_unit_1: pin names not known; wires that end beside it: Z, {control_unit_1_p2_2, control_unit_1_p2}, DMUX, ALUOP, RS1, RS2, WS, WE, EXEC, SETH, FLEN, STR, LDR, I_mem
  Multiplexer #(.Selector_Bits(2), .Bits(16)) multiplexer_1 (
    .sel(DMUX), .in_0(alu_1_result), .in_1(RAM_d1), .in_2({{8{1'b0}}, control_unit_1_p2}),
    .in_3(notconnected_1_out), .out(multiplexer_1_out));
  // NotConnected on notconnected_1_out
  reg_file reg_file_1 (
    .IN(multiplexer_1_out), .clk(CLK), .RS1(RS1), .RS2(RS2), .WS(WS), .WE(WE), .EXEC(EXEC), .SETH(SETH),
    .FLIN({FL_q, Z}), .OUT1(reg_file_1_out1), .OUT2(reg_file_1_out2), .PC(reg_file_1_pc));
  RAMDualAccess #(.AddrBits(16), .isProgramMemory("true"), .Bits(16)) RAM (
    .str(STR), .C(CLK), .ld(LDR), .A1(i_mem_1__1a), .Din1(reg_file_1_out2), .A2(reg_file_1_pc), .D1(RAM_d1),
    .D2({control_unit_1_p2_2, control_unit_1_p2}));
  I_mem i_mem_1 (.o1(reg_file_1_out1), .en(I_mem), .inst({control_unit_1_p2_2, control_unit_1_p2}), ._1a(i_mem_1__1a));
  alu alu_1 (.A(reg_file_1_out1), .B(reg_file_1_out2), .RESULT(alu_1_result), .ALUOP(ALUOP), .FLAG(alu_1_flag));
  Register #(.Bits(16)) FL (.D({{12{1'b0}}, alu_1_flag}), .C(CLK), .en(FLEN), .Q({FL_q, Z}));
endmodule
